# Fritzing sketch Untitled Sketch 3 (saved by Fritzing 0.9.3b)
circuit board: 8.46667cm x 5.64444cm
breadboards: 1

parts:
  LED12 = LED - 3mm [color="Blue (430nm)" package="3 mm [THT]"]
  R21 = Resistor [tolerance=±5% resistance=150 power=0pW package=THT]
  R4 = Resistor [tolerance=±5% resistance=1k package=THT]
  R11 = Resistor [tolerance=±5% resistance=1k package=THT]
  R13 = Resistor [tolerance=±5% resistance=1k package=THT]
  R10 = Resistor [tolerance=±5% resistance=1k package=THT]
  LED10 = LED - 3mm [color="Blue (430nm)" package="3 mm [THT]"]
  R15 = Resistor [tolerance=±5% resistance=150 power=0pW package=THT]
  LED8 = LED - 3mm [color="Blue (430nm)" package="3 mm [THT]"]
  R19 = Resistor [tolerance=±5% resistance=150 power=0pW package=THT]
  LED7 = LED - 3mm [color="Blue (430nm)" package="3 mm [THT]"]
  LED6 = LED - 3mm [color="Blue (430nm)" package="3 mm [THT]"]
  R7 = Resistor [tolerance=±5% resistance=1k package=THT]
  R2 = Resistor [tolerance=±5% resistance=150 power=5W package=THT]
  LED5 = LED - 3mm [color="Blue (430nm)" package="3 mm [THT]"]
  Componente1 = Arduino Uno (Rev3)
  R6 = Resistor [tolerance=±5% resistance=1k package=THT]
  R17 = Resistor [tolerance=±5% resistance=150 power=0pW package=THT]
  R5 = Resistor [tolerance=±5% resistance=1k package=THT]
  R8 = Resistor [tolerance=±5% resistance=1k package=THT]
  R23 = Resistor [tolerance=±5% resistance=150 power=0pW package=THT]
  LED9 = LED - 3mm [color="Blue (430nm)" package="3 mm [THT]"]
  R18 = Resistor [tolerance=±5% resistance=150 power=0pW package=THT]
  LED3 = LED - 3mm [color="Blue (430nm)" package="3 mm [THT]"]
  LED11 = LED - 3mm [color="Blue (430nm)" package="3 mm [THT]"]
  LED2 = LED - 3mm [color="Blue (430nm)" package="3 mm [THT]"]
  R22 = Resistor [tolerance=±5% resistance=150 power=0pW package=THT]
  R9 = Resistor [tolerance=±5% resistance=1k package=THT]
  R1 = Resistor [tolerance=±5% resistance=1k package=THT]
  R12 = Resistor [tolerance=±5% resistance=1k package=THT]
  R20 = Resistor [tolerance=±5% resistance=150 power=0pW package=THT]
  R16 = Resistor [tolerance=±5% resistance=150 power=0pW package=THT]
  R14 = Resistor [tolerance=±5% resistance=1k package=THT]
  LED4 = LED - 3mm [color="Blue (430nm)" package="3 mm [THT]"]
  LED1 = LED - 3mm [color="Blue (430nm)" package="3 mm [THT]"]
  R24 = Resistor [tolerance=±5% resistance=150 power=0pW package=THT]
  R3 = Resistor [tolerance=±5% resistance=150 power=0pW package=THT]

nets:
  N1: LED12.cathode, R4.Pin_1, R11.Pin_1, R13.Pin_1, R10.Pin_1, LED10.cathode, LED8.cathode, LED7.cathode, LED6.cathode, R7.Pin_1, LED5.cathode, Componente1.GND, R6.Pin_1, R5.Pin_1, R8.Pin_1, LED9.cathode, LED3.cathode, LED11.cathode, LED2.cathode, R9.Pin_1, R1.Pin_1, R12.Pin_1, R14.Pin_1, LED4.cathode, LED1.cathode
  N2: LED12.anode, R24.Pin_0
  N3: R21.Pin_0, LED9.anode
  N4: R21.Pin_1, R11.Pin_0, Componente1.D5_PWM
  N5: R4.Pin_0, Componente1.D12/MISO, R3.Pin_1
  N6: R13.Pin_0, Componente1.D3_PWM, R23.Pin_1
  N7: R10.Pin_0, Componente1.D6_PWM, R20.Pin_1
  N8: LED10.anode, R22.Pin_0
  N9: R15.Pin_0, LED3.anode
  N10: R15.Pin_1, Componente1.D11_PWM/MOSI, R5.Pin_0
  N11: LED8.anode, R20.Pin_0
  N12: R19.Pin_0, LED7.anode
  N13: R19.Pin_1, Componente1.D7, R9.Pin_0
  N14: LED6.anode, R18.Pin_0
  N15: R7.Pin_0, Componente1.D9_PWM, R17.Pin_1
  N16: R2.Pin_0, LED1.anode
  N17: R2.Pin_1, Componente1.D13/SCK, R1.Pin_0
  N18: LED5.anode, R17.Pin_0
  N19: Componente1.D8, R8.Pin_0, R18.Pin_1
  N20: Componente1.D10_PWM/SS, R6.Pin_0, R16.Pin_1
  N21: Componente1.D2, R14.Pin_0, R24.Pin_1
  N22: Componente1.D4, R22.Pin_1, R12.Pin_0
  N23: R23.Pin_0, LED11.anode
  N24: LED2.anode, R3.Pin_0
  N25: R16.Pin_0, LED4.anode
